// Digital circuit MUX8_1.dig as structural Verilog
module MUX8_1 (
  input  s2,
  input  s1,
  input  s0,
  input  d1,
  input  d0,
  input  d2,
  input  d3,
  input  d4,
  input  d5,
  input  d6,
  input  d7,
  output y
);

  wire and_1_out, and_2_out, and_3_out, and_4_out, and_5_out, and_6_out, and_7_out, and_8_out, not_1_out,
       not_2_out, not_3_out;

  not not_1 (not_1_out, s2);
  not not_2 (not_2_out, s1);
  not not_3 (not_3_out, s0);
  and and_1 (and_1_out, not_1_out, not_2_out, not_3_out, d0);
  and and_2 (and_2_out, not_1_out, not_2_out, s0, d1);
  and and_3 (and_3_out, not_1_out, s1, not_3_out, d2);
  and and_4 (and_4_out, not_1_out, s1, s0, d3);
  and and_5 (and_5_out, s2, not_2_out, not_3_out, d4);
  and and_6 (and_6_out, s2, not_2_out, s0, d5);
  and and_7 (and_7_out, s2, s1, not_3_out, d6);
  and and_8 (and_8_out, s2, s1, s0, d7);
  or or_1 (y, and_1_out, and_2_out, and_3_out, and_4_out, and_5_out, and_6_out, and_7_out, and_8_out);
endmodule
