// Digital circuit Practica guiada 1.dig as structural Verilog
module Practica_guiada_1 (
  input  A,
  input  B,
  input  C,
  output SOP,
  output POS
);

  wire and_1_out, and_2_out, not_1_out, not_2_out, not_3_out, or_1_out, or_2_out;

  not not_1 (not_1_out, A);
  not not_2 (not_2_out, B);
  not not_3 (not_3_out, C);
  and and_1 (and_1_out, not_1_out, not_3_out);
  and and_2 (and_2_out, B, C);
  or or_1 (or_1_out, B, not_3_out);
  or or_2 (or_2_out, not_1_out, C);
  or or_3 (SOP, and_1_out, and_2_out);
  and and_3 (POS, or_1_out, or_2_out);
endmodule
