// Digital circuit Practica guiada 2.dig as structural Verilog
module Practica_guiada_2 (
  input  A,
  input  B,
  input  C,
  input  D,
  output Canonica_SP,
  output SP,
  output NAND
);

  wire and_1_out, and_2_out, and_3_out, and_4_out, and_5_out, and_6_out, and_7_out, and_8_out, and_9_out,
       and_10_out, and_11_out, nand_1_out, nand_2_out, nand_3_out, not_1_out, not_2_out, not_3_out, not_4_out;

  not not_1 (not_1_out, A);
  not not_2 (not_2_out, B);
  not not_3 (not_3_out, C);
  nand nand_1 (nand_1_out, C, C);
  not not_4 (not_4_out, D);
  and and_1 (and_1_out, not_1_out, not_2_out, not_3_out, not_4_out);
  and and_2 (and_2_out, not_1_out, not_2_out, not_3_out, D);
  and and_3 (and_3_out, not_1_out, not_2_out, C, not_4_out);
  and and_4 (and_4_out, not_1_out, not_2_out, C, D);
  and and_5 (and_5_out, not_1_out, B, not_3_out, not_4_out);
  and and_6 (and_6_out, not_1_out, B, not_3_out, D);
  and and_7 (and_7_out, not_1_out, B, C, not_4_out);
  and and_8 (and_8_out, not_1_out, B, C, D);
  and and_9 (and_9_out, A, B, not_3_out, not_4_out);
  and and_10 (and_10_out, not_1_out, not_1_out);
  and and_11 (and_11_out, B, not_3_out, not_4_out);
  nand nand_2 (nand_2_out, D, D);
  nand nand_3 (nand_3_out, B, nand_1_out, nand_2_out);
  nand nand_4 (NAND, A, nand_3_out);
  or or_1 (Canonica_SP, and_1_out, and_2_out, and_3_out, and_4_out, and_5_out, and_6_out, and_7_out, and_8_out, and_9_out);
  or or_2 (SP, and_10_out, and_11_out);
endmodule
