// Digital circuit Practica guiada 3.dig as structural Verilog
module Practica_guiada_3 (
  input  X3,
  input  X2,
  input  X1,
  input  X0,
  output B
);

  wire not_1_out;

  not not_1 (not_1_out, X0);
  MUX8_1 mux8_1_1 (
    .s2(X3), .s1(X2), .s0(X1), .d1(X0), .d0(1'b0), .d2(1'b0), .d3(not_1_out), .d4(X0), .d5(1'b0),
    .d6(not_1_out), .d7(X0), .y(B));
endmodule
