// Digital circuit Practica guiada 4.dig as structural Verilog
module Practica_guiada_4 (
  input  a,
  input  b,
  input  c,
  input  d,
  output _4B,
  output _4A,
  output _4C
);

  wire and_1_out, and_2_out, and_3_out, and_4_out, decoder_1_out_2, decoder_1_out_5, decoder_1_out_7,
       decoder_1_out_13, decoder_1_out_14, not_1_out, not_2_out, not_3_out, not_4_out;

  not not_1 (not_1_out, a);
  not not_2 (not_2_out, b);
  not not_3 (not_3_out, c);
  not not_4 (not_4_out, d);
  and and_1 (and_1_out, not_1_out, not_2_out, c, not_4_out);
  and and_2 (and_2_out, not_1_out, b, d);
  and and_3 (and_3_out, b, not_3_out, d);
  and and_4 (and_4_out, a, b, c, not_4_out);
  or or_1 (_4A, and_1_out, and_2_out, and_3_out, and_4_out);
  Multiplexer #(.Selector_Bits(3)) multiplexer_1 (
    .sel({a, b, c}), .in_0(1'b0), .in_1(not_4_out), .in_2(d), .in_3(d), .in_4(1'b0), .in_5(1'b0), .in_6(d),
    .in_7(not_4_out), .out(_4C));
  Decoder #(.Selector_Bits(4)) decoder_1 (
    .sel({a, b, c, d}), .out_2(decoder_1_out_2), .out_5(decoder_1_out_5), .out_7(decoder_1_out_7),
    .out_13(decoder_1_out_13), .out_14(decoder_1_out_14));  // open: out_0, out_1, out_3, out_4, out_6, out_8, out_9, out_10, out_11, out_12, out_15
  or or_2 (_4B, decoder_1_out_2, decoder_1_out_5, decoder_1_out_7, decoder_1_out_13, decoder_1_out_14);
endmodule
